// Logisim project cpu.circ as structural Verilog: 1 circuit, main circuit main
// 1
module main (
  input  [31:0] INSTRUCTION,
  input  CLOCK,
  output [31:0] FETCH_ADDRESS,
  output [31:0] s0_Value,
  output [31:0] s1_Value,
  output [31:0] s2_Value,
  output [31:0] ra_Value,
  output [31:0] sp_Value
);

  wire add, addi, addiu, addu, ALUSrc, \and , and_6_out, and_7_out, and_8_out, and_9_out, andi, beq, bltzal,
       bne, Branch, isOp1, isOp2, isR, isR1, isR2, j, jal, jr, Jump, KillNext, KillThis, link, lui, lw,
       MemWrite, not_1_out, not_2_out, not_4_out, not_5_out, \or , or_3_out, or_4_out, or_5_out, or_6_out,
       or_7_out, or_8_out, ori, RegWrite, sll, slt, slti, sltiu, sltu, sra, srl, tunnel;
  wire [3:0] ALUOP, multiplexer_4_out, multiplexer_5_out, multiplexer_6_out, multiplexer_7_out,
       multiplexer_8_out, multiplexer_9_out, multiplexer_10_out, multiplexer_11_out;
  wire [4:0] demultiplexer_1_out0, demultiplexer_1_out1, demultiplexer_2_out0, demultiplexer_2_out1,
       multiplexer_14_out;
  wire [5:0] funct;
  wire [15:0] linkInstruction;
  wire [15:6] immediate;
  wire [31:0] ALUR, and_2_out, BDest, instruction2, jAddr, jrAddr, MemOut, multiplexer_1_out,
       multiplexer_2_out, multiplexer_12_out, multiplexer_15_out, multiplexer_16_out, multiplexer_17_out,
       or_1_out, RD2, shifter_1_out;
  wire [31:16] instructionPK, PC_4;

  Demultiplexer #(.width(5)) demultiplexer_1 (
    .out0(demultiplexer_1_out0), .out1(demultiplexer_1_out1), .in(funct[4:0]), .sel(funct[5]), .en(isR));
  and and_1 (isR2, funct[5], isR);
  Multiplexer #(.width(32), .disabled(0), .enable("false")) multiplexer_1 (
    .in0({PC_4, linkInstruction}), .in1(BDest), .out(multiplexer_1_out), .sel(Branch));
  assign and_2_out = {PC_4, linkInstruction} & 32'hf0000000;  // AND_Gate and_2, 32 bits wide
  Comparator #(.width(6)) comparator_1 (.a(instructionPK[31:26]), .b({6{1'b0}}), .eq(isR));  // open: gt, lt
  Decoder #(.select(5), .disabled(0)) decoder_1 (
    .out0(sll), .out2(srl), .out3(sra), .out8(jr), .sel(demultiplexer_1_out0), .en(isR1));  // open: out1, out4, out5, out6, out7, out9, out10, out11, out12, out13, out14, out15, out16, out17, out18, out19, out20, out21, out22, out23, out24, out25, out26, out27, out28, out29, out30, out31
  not not_1 (not_1_out, isR2);
  and and_3 (isR1, not_1_out, isR);
  Register #(.width(32)) PC (.D(multiplexer_2_out), .Q(FETCH_ADDRESS), .clk(CLOCK));  // open: en, clr
  Multiplexer #(.width(32), .disabled(0), .enable("false")) multiplexer_2 (
    .in0(multiplexer_1_out), .in1(jAddr), .out(multiplexer_2_out), .sel(Jump));
  assign or_1_out = and_2_out | {4'b0000, instructionPK[25:16], immediate, funct, 2'b00};  // OR_Gate or_1, 32 bits wide
  Multiplexer #(.width(32), .disabled(0), .enable("false")) multiplexer_3 (
    .in0(or_1_out), .in1(jrAddr), .out(jAddr), .sel(jr));
  Decoder #(.select(5), .disabled(0)) decoder_2 (
    .out0(add), .out1(addu), .out4(\and ), .out5(\or ), .out10(slt), .out11(sltu),
    .sel(demultiplexer_1_out1), .en(isR2));  // open: out2, out3, out6, out7, out8, out9, out12, out13, out14, out15, out16, out17, out18, out19, out20, out21, out22, out23, out24, out25, out26, out27, out28, out29, out30, out31
  Demultiplexer #(.width(5)) demultiplexer_2 (
    .out0(demultiplexer_2_out0), .out1(demultiplexer_2_out1), .in(instructionPK[30:26]),
    .sel(instructionPK[31]), .en(not_2_out));
  and and_4 (isOp2, instructionPK[31], not_2_out);
  not not_2 (not_2_out, isR);
  Adder #(.width(32)) adder_1 (.a(FETCH_ADDRESS), .b(32'h4), .out({PC_4, linkInstruction}));  // open: cin, cout
  not not_3 (ALUSrc, isR);
  Decoder #(.select(5), .disabled(0)) decoder_3 (
    .out1(bltzal), .out2(j), .out3(jal), .out4(beq), .out5(bne), .out8(addi), .out9(addiu), .out10(slti),
    .out11(sltiu), .out12(andi), .out13(ori), .out15(lui), .sel(demultiplexer_2_out0), .en(isOp1));  // open: out0, out6, out7, out14, out16, out17, out18, out19, out20, out21, out22, out23, out24, out25, out26, out27, out28, out29, out30, out31
  not not_4 (not_4_out, isOp2);
  and and_5 (isOp1, not_4_out, not_5_out);
  not not_5 (not_5_out, isR);
  or or_2 (Jump, jr, jal, j);
  or Tweet (RegWrite, srl, sll, sra, add, addu, sltu, sltiu, \or , addi, slt, slti, \and , andi, ori, lui, lw, addiu);
  Decoder #(.select(5), .disabled(0)) decoder_4 (
    .out3(lw), .out11(MemWrite), .sel(demultiplexer_2_out1), .en(isOp2));  // open: out0, out1, out2, out4, out5, out6, out7, out8, out9, out10, out12, out13, out14, out15, out16, out17, out18, out19, out20, out21, out22, out23, out24, out25, out26, out27, out28, out29, out30, out31
  or or_3 (or_3_out, addu, addiu);
  or or_4 (or_4_out, add, addi);
  or or_5 (or_5_out, \and , andi);
  or or_6 (or_6_out, \or , ori);
  or or_7 (or_7_out, slti, slt);
  or or_8 (or_8_out, sltiu, sltu);
  or or_9 (KillNext, Jump, Branch);
  Multiplexer #(.width(4), .disabled(0), .enable("false")) multiplexer_4 (
    .in0(4'b0000), .in1(4'b0001), .out(multiplexer_4_out), .sel(srl));
  Multiplexer #(.width(4), .disabled(0), .enable("false")) multiplexer_5 (
    .in0(4'b0000), .in1(4'b0010), .out(multiplexer_5_out), .sel(sra));
  Multiplexer #(.width(4), .disabled(0), .enable("false")) multiplexer_6 (
    .in0(4'b0000), .in1(4'b0110), .out(multiplexer_6_out), .sel(or_3_out));
  Multiplexer #(.width(4), .disabled(0), .enable("false")) multiplexer_7 (
    .in0(4'b0000), .in1(4'b0101), .out(multiplexer_7_out), .sel(or_4_out));
  Multiplexer #(.width(4), .disabled(0), .enable("false")) multiplexer_8 (
    .in0(4'b0000), .in1(4'b1001), .out(multiplexer_8_out), .sel(or_5_out));
  Multiplexer #(.width(4), .disabled(0), .enable("false")) multiplexer_9 (
    .in0(4'b0000), .in1(4'b1010), .out(multiplexer_9_out), .sel(or_6_out));
  Multiplexer #(.width(4), .disabled(0), .enable("false")) multiplexer_10 (
    .in0(4'b0000), .in1(4'b1110), .out(multiplexer_10_out), .sel(or_7_out));
  Multiplexer #(.width(4), .disabled(0), .enable("false")) multiplexer_11 (
    .in0(4'b0000), .in1(4'b1111), .out(multiplexer_11_out), .sel(or_8_out));
  and and_6 (and_6_out, beq, tunnel);
  or or_10 (Branch, and_6_out, and_7_out, and_8_out);
  and and_7 (and_7_out, bne, ~tunnel);  // AND_Gate
  and and_8 (and_8_out, bltzal, ALUR[31]);
  D_Flip_Flop Kill (.clk(CLOCK), .D(KillNext), .Q(KillThis), .preset(1'b0), .en(1'b1), .reset(1'b0));  // open: Qn
  Multiplexer #(.width(32), .disabled(0), .enable("false")) multiplexer_12 (
    .in0({32{1'b0}}), .in1({16'h8f0, linkInstruction}), .out(multiplexer_12_out), .sel(link));
  assign ALUOP = multiplexer_4_out | multiplexer_5_out | multiplexer_6_out | multiplexer_7_out | multiplexer_8_out | multiplexer_9_out | multiplexer_10_out | multiplexer_11_out;  // OR_Gate Octopussy, 4 bits wide
  Multiplexer #(.width(32), .disabled(0), .enable("false")) multiplexer_13 (
    .in0(instruction2), .in1(multiplexer_12_out), .out({instructionPK, immediate, funct}), .sel(KillThis));
  Register #(.width(32)) Instruction_delay (.D(INSTRUCTION), .Q(instruction2), .clk(CLOCK));  // open: en, clr
  and and_9 (and_9_out, bltzal, ALUR[31]);
  Shifter #(.width(32)) shifter_1 (
    .in({{17{immediate[15]}}, immediate[14:6], funct}), .\dist (5'b00010), .out(shifter_1_out));
  or or_11 (link, and_9_out, jal);
  Adder #(.width(32)) adder_2 (.a({PC_4, linkInstruction}), .b(shifter_1_out), .out(BDest));  // open: cin, cout
  Multiplexer #(.width(5), .disabled(0), .enable("false")) multiplexer_14 (
    .in0(instructionPK[20:16]), .in1(immediate[15:11]), .out(multiplexer_14_out), .sel(isR));
  Multiplexer #(.width(32), .disabled(0), .enable("false")) multiplexer_15 (
    .in0(ALUR), .in1(MemOut), .out(multiplexer_15_out), .sel(lw));
  regfile_main main_1 (
    .Read_Register_1(instructionPK[25:21]), .Read_Register_2(instructionPK[20:16]),
    .Write_Register(multiplexer_14_out), .Write_Data(multiplexer_16_out), .Write_Enable(RegWrite),
    .Clock(CLOCK), .Read_Data_1(jrAddr), .Read_Data_2(RD2), .s0_Value(s0_Value), .s1_Value(s1_Value),
    .s2_Value(s2_Value), .ra_Value(ra_Value), .sp_Value(sp_Value));
  Multiplexer #(.width(32), .disabled(0), .enable("false")) multiplexer_16 (
    .in0(multiplexer_15_out), .in1({immediate, funct, {16{1'b0}}}), .out(multiplexer_16_out), .sel(lui));
  alu_main main_2 (
    .Switch(ALUOP), .X(jrAddr), .Equal(tunnel), .Result(ALUR), .Y(multiplexer_17_out));  // open: Signed_Overflow
  Multiplexer #(.width(32), .disabled(0), .enable("false")) multiplexer_17 (
    .in0(RD2), .in1({{17{immediate[15]}}, immediate[14:6], funct}), .out(multiplexer_17_out), .sel(ALUSrc));
  // mem_main main_3: pin names not known; wires that end beside it: ALUR, RD2, MemWrite, CLOCK, MemOut

  // Other names for the same wires on the sheet: clk = CLOCK; fetch_addr[31:0] = FETCH_ADDRESS;
  //   PC[31:0] = FETCH_ADDRESS; op[5:0] = instructionPK[31:26]; RegDest = isR; PC_4[15:0] = linkInstruction;
  //   MemRead = lw; MemToReg = lw; preAddr[27:2] = {instructionPK[25:16], immediate, funct};
  //   rt[4:0] = instructionPK[20:16]; rs[4:0] = instructionPK[25:21]; ra[31:0] = ra_Value; s0[31:0] = s0_Value;
  //   s1[31:0] = s1_Value; s2[31:0] = s2_Value; sp[31:0] = sp_Value; sw = MemWrite; immediate[5:0] = funct;
  //   instructionPK[15:0] = {immediate, funct}; SEI[31:0] = {{17{immediate[15]}}, immediate[14:6], funct};
  //   upperImmediate[31:16] = {immediate, funct}; shamt[4:0] = immediate[10:6]; rd[4:0] = immediate[15:11]

  // Notes on the sheet:
  //   Output
  //   These are outputs/inputs from run.circ
  //   Inputs
  //   These are DEBUG/TEST outputs from your circuit.
endmodule
