// Logisim project regfile-testAllRegs.circ as structural Verilog: 1 circuit, main circuit main
module main (
  output [7:0] test_num,
  output [31:0] Reg_0_Value,
  output [31:0] Reg_1_Value,
  output [31:0] Reg_2_Value,
  output [31:0] Reg_3_Value,
  output [31:0] Reg_4_Value,
  output halt,
  output [31:0] Read_Data_1,
  output [31:0] Read_Data_2
);

  wire clock_1_out;
  wire [7:0] adder_1_out;
  wire [15:0] rom_2_data;
  wire [31:0] WriteData;

  Register register_1 (.D(adder_1_out), .en(1'b1), .Q(test_num), .clk(clock_1_out));  // open: clr
  Adder adder_1 (.a(8'h1), .b(test_num), .out(adder_1_out));  // open: cin, cout
  Comparator #(.mode("unsigned")) comparator_1 (.a(8'h5), .b(test_num), .eq(halt));  // open: gt, lt
  ROM #(.dataWidth(32)) rom_1 (.addr(test_num), .data(WriteData));  // open: sel
  ROM #(.dataWidth(16)) rom_2 (.addr(test_num), .data(rom_2_data), .sel(1'b1));
  Clock clock_1 (.out(clock_1_out));
  regfile_main main_1 (
    .Read_Register_1(rom_2_data[4:0]), .Read_Register_2(rom_2_data[9:5]), .Write_Register(rom_2_data[14:10]),
    .Write_Data(WriteData), .Write_Enable(rom_2_data[15]), .Clock(clock_1_out), .Read_Data_1(Read_Data_1),
    .Read_Data_2(Read_Data_2), .s0_Value(Reg_0_Value), .s1_Value(Reg_1_Value), .s2_Value(Reg_2_Value),
    .ra_Value(Reg_3_Value), .sp_Value(Reg_4_Value));

  // Notes on the sheet:
  //   contents of rom_1 (hex, n*v repeats v):
  //   1 2 3 4 5 6 7 8 9 a b c d e 10 11 12 13 14 15 16 17 18 19 1a 1b 1c
  //   contents of rom_2 (hex, n*v repeats v):
  //   8400 8800 8C00 9000 9400 9800 9C00 A000 A400 A800 AC00 B000 B400 B800 BC00 C400 C800 CC00 D000 D400
  //   D800 DC00 E000 E400 E800 EC00 F000 F400 F800 FC00 2000 4000 6000 8000 A000 C000 E000 8000 9000 A000
  //   B000 C000 D000 E000 F000 8800 9000 9800 A000 A800 B000 B800 C000 C800 D000 D800 E000 E800 F000 F800
  //   YOUR REGFILE SHOULD FIT IN HERE!
  //   There should be no blue/red wires here, and the result shouldn't be x's.
endmodule
